# Fritzing sketch Infrared_RPi (saved by Fritzing 0.9.2b)
breadboards: 1

parts:
  Raspberry_Pi1 = Raspberry Pi 2
  R1 = Resistor [tolerance=±5% resistance=56 package=THT]
  Q1 = NPN-Transistor [package="TO92 [THT]"]
  LED1 = LED - 5mm [color="Infrared (940nm)" package="5 mm [THT]"]
  R2 = Resistor [tolerance=±5% resistance=12k package=THT]
  IR1 = TSOP312.., 314.. [package=THT]
  R3 = Resistor [tolerance=±5% resistance=220 package=THT]

nets:
  N1: Raspberry_Pi1.3v3, R3.Pin_1
  N2: Raspberry_Pi1.GPIO22, IR1.GND
  N3: Raspberry_Pi1.GND, Q1.E, IR1.Vs
  N4: Raspberry_Pi1.GPIO23, R2.Pin_0
  N5: Raspberry_Pi1.5V, R1.Pin_0
  N6: R1.Pin_1, LED1.anode
  N7: Q1.B, R2.Pin_1
  N8: Q1.C, LED1.cathode
  N9: IR1.Data, R3.Pin_0

notes:
  réception - 3.3V
  emission - 5V
